// Logisim project Aux1.circ as structural Verilog: 2 circuits, main circuit SegD
module SegD (
  input  x3,
  input  x2,
  input  x1,
  input  x0,
  output d
);

  wire and_1_out, and_2_out, and_3_out, and_4_out, not_1_out, not_2_out, not_3_out;

  not not_1 (not_1_out, x0);
  not not_2 (not_2_out, x1);
  not not_3 (not_3_out, x2);
  and and_1 (and_1_out, x2, not_2_out, x0);
  and and_2 (and_2_out, not_1_out, x1);
  and and_3 (and_3_out, not_3_out, x1);
  and and_4 (and_4_out, not_3_out, not_1_out);
  or or_1 (d, x3, and_1_out, and_2_out, and_3_out, and_4_out);
endmodule

module _7segms (
  input  in_1,
  input  in_2,
  input  in_3,
  input  in_4
);

  wire segd_1_d;

  LED led_1 (.in(segd_1_d));
  SegD segd_1 (.x3(in_1), .x2(in_2), .x1(in_3), .x0(in_4), .d(segd_1_d));
endmodule
